# Fritzing sketch chargecap (saved by Fritzing 1.0.6)
circuit board: 12.1994cm x 8.01074cm

parts:
  A1 = Esp32-c3 super mini
  Grove1 = Grove OLED 128x96
  A2 = mosfet switch HW-548 modified pcb
  AMS1 = AMS1777 5V regulator module
  X1 = USB Connectors [package=usb-a-s-silk-female]
  J2 = USB_3.1_typeC_usb_connector-amphenol [package=SMD]
  Part1 = Adafruit USB Type C Breakout [part_number=4090]
  S1 = SWITCH-MOMENTARY-2 [package=tactile-pth-12mm]
  C1 = Capacitor [package=cap-pth-small2]
  C2 = Capacitor Polarized [package=panasonic_c]
  Z1 = VARISTOR [package=0402-res]
  R1 = Resistor [tolerance=±5% power=0.25W resistance=220 package=THT]

nets (from the breadboard view):
  N1: A1.Pin_2, Grove1.SCL
  N2: A1.Pin_3, Grove1.SDA
  N3: A1.Pin_4, S1.1
  N4: A1.Pin_14, Grove1.VCC, AMS1.VOUT+, S1.2, C2.+
  N5: A1.Pin_15, Grove1.GND, AMS1.GND-_(output), C2.-, R1.Pin_1
  N6: A2.Pin_4, A2.Pin_7, C1.1, Z1.2
  N7: A2.Pin_10, X1.GND, J2.pin_B12
  N8: AMS1.VIN+, X1.VBUS, Part1.VBUS
  N9: AMS1.GND-_(input), Part1.GND
  N10: J2.pin_B8, Part1.CC1
  N11: J2.pin_B7, Part1.D+
  N12: J2.pin_B6, Part1.D-
  N13: J2.pin_B5, Part1.SBU1
  N14: J2.pin_A8, Part1.CC2
  N15: J2.pin_A5, Part1.SBU2
  N16: C1.2, Z1.1

custom parts:
  Esp32-c3 super mini: ESP32-C3 Development Board ESP32 SuperMini Development Board ESP32 Development Board WiFi Bluetooth.
  mosfet switch HW-548 modified pcb: #548 Electronic switch control board pulse trigger switch DC controller module Field effect transistor power module. (Oct 2023 modified pcb to add pads for 4 of the terminal blocks.)
  AMS1777 5V regulator module: AMS1777 5V regulator module source : https://github.com/ShenTengTu/fritzing_parts/tree/master/voltage%20regulator/AMS1117_5V_regulator_module
  USB_3.1_typeC_usb_connector-amphenol: Am[henol right angle usb 3.1 typc C USB connector receptacle Surface Mount.
  Adafruit USB Type C Breakout: Adafruit breakout board for USB Type C socket.
